// Logisim project FULL ADDER.circ as structural Verilog: 1 circuit, main circuit main
module main (
  input  in_1,
  input  in_2,
  input  in_3,
  input  in_4,
  input  in_5,
  input  in_6,
  input  in_7,
  input  in_8,
  input  in_9,
  input  in_10,
  input  in_11,
  input  in_12,
  input  in_13,
  input  in_14,
  input  in_15,
  input  in_16,
  input  in_17,
  input  in_18,
  input  in_19,
  input  in_20,
  input  in_21,
  input  in_22,
  input  in_23,
  input  in_24,
  output out_25,
  output out_26,
  output out_27,
  output out_28,
  output out_29,
  output out_30,
  output out_31,
  output out_32,
  output out_33,
  output out_34,
  output out_35,
  output out_36,
  output out_37,
  output out_38,
  output out_39,
  output out_40
);

  wire and_1_out, and_2_out, and_3_out, and_4_out, and_5_out, and_6_out, and_7_out, and_8_out, and_9_out,
       and_10_out, and_11_out, and_12_out, and_13_out, and_14_out, and_15_out, and_16_out, xor_1_out,
       xor_2_out, xor_3_out, xor_4_out, xor_9_out, xor_10_out, xor_11_out, xor_12_out;

  xor xor_1 (xor_1_out, in_2, in_4);
  and and_1 (and_1_out, in_2, in_4);
  xor xor_2 (xor_2_out, in_7, in_9);
  and and_2 (and_2_out, in_7, in_9);
  xor xor_3 (xor_3_out, in_13, in_15);
  and and_3 (and_3_out, in_13, in_15);
  xor xor_4 (xor_4_out, in_20, in_22);
  and and_4 (and_4_out, in_20, in_22);
  xor xor_5 (out_26, xor_1_out, in_6);
  xor xor_6 (out_29, xor_2_out, in_11);
  xor xor_7 (out_33, xor_3_out, in_17);
  xor xor_8 (out_38, xor_4_out, in_24);
  and and_5 (and_5_out, xor_1_out, in_6);
  or or_1 (out_28, and_5_out, and_1_out);
  and and_6 (and_6_out, xor_2_out, in_11);
  or or_2 (out_31, and_6_out, and_2_out);
  and and_7 (and_7_out, xor_3_out, in_17);
  or or_3 (out_35, and_7_out, and_3_out);
  and and_8 (and_8_out, xor_4_out, in_24);
  or or_4 (out_40, and_8_out, and_4_out);
  xor xor_9 (xor_9_out, in_1, in_3);
  and and_9 (and_9_out, in_1, in_3);
  xor xor_10 (xor_10_out, in_8, in_10);
  and and_10 (and_10_out, in_8, in_10);
  xor xor_11 (xor_11_out, in_14, in_16);
  and and_11 (and_11_out, in_14, in_16);
  xor xor_12 (xor_12_out, in_19, in_21);
  and and_12 (and_12_out, in_19, in_21);
  xor xor_13 (out_25, xor_9_out, in_5);
  xor xor_14 (out_30, xor_10_out, in_12);
  xor xor_15 (out_34, xor_11_out, in_18);
  xor xor_16 (out_37, xor_12_out, in_23);
  and and_13 (and_13_out, xor_9_out, in_5);
  or or_5 (out_27, and_13_out, and_9_out);
  and and_14 (and_14_out, xor_10_out, in_12);
  or or_6 (out_32, and_14_out, and_10_out);
  and and_15 (and_15_out, xor_11_out, in_18);
  or or_7 (out_36, and_15_out, and_11_out);
  and and_16 (and_16_out, xor_12_out, in_23);
  or or_8 (out_39, and_16_out, and_12_out);
endmodule
