// Logisim project HALF ADDER.circ as structural Verilog: 1 circuit, main circuit main
module main (
  input  in_1,
  input  in_2,
  input  in_3,
  input  in_4,
  input  in_5,
  input  in_6,
  input  in_7,
  input  in_8,
  output out_9,
  output out_10,
  output out_11,
  output out_12,
  output out_13,
  output out_14,
  output out_15,
  output out_16
);

  xnor xnor_1 (out_9, in_1, in_2);
  buf and_1 (out_11, in_1);  // AND_Gate
  buf and_2 (out_15, in_5);  // AND_Gate
  xnor xnor_2 (out_13, in_5, in_6);
  buf and_3 (out_12, in_3);  // AND_Gate
  xnor xnor_3 (out_10, in_3, in_4);
  xnor xnor_4 (out_14, in_7, in_8);
  buf and_4 (out_16, in_7);  // AND_Gate
endmodule
