// Logisim project NOT GATE.circ as structural Verilog: 1 circuit, main circuit main
module main (
  input  in_1,
  input  in_2,
  output out_3,
  output out_4
);

  not not_1 (out_4, in_2);
  not not_2 (out_3, in_1);
endmodule
